# Fritzing sketch Flameduino (saved by Fritzing 0.9.2b)
circuit board: 6.88566cm x 5.36311cm
breadboards: 1

parts:
  Arduino = Arduino Uno (Rev3)
  VReg = Voltage Regulator - 5V [package="TO220 [THT]"]
  BIP373 = Basic FET P-Channel [package="TO220 [THT]"]
  Vin = Screw terminal - 2 pins [package=THT]
  Frequency = screw terminal, 3 pins
  Coil = screw terminal, 3 pins
  Activation = screw terminal, 3 pins
  Vehicle = Screw terminal - 2 pins [package=THT]
  Qinterrupt = NPN-Transistor [package="TO92 [THT]"]
  LED = LED - 5mm [color="Red (633nm)" package="5 mm [THT]"]
  Rled = Resistor [tolerance=±5% resistance=330 package=THT]
  Pad1 = Pad [width=12 height=18 connect=center]
  Pad2 = Pad [width=12 height=18 connect=center]
  JMP = male pin header, 2 pins [form="♂ (male)"]

nets:
  N1: Arduino.A0, Frequency.pin2
  N2: Arduino.D8, Coil.pin1
  N3: Arduino.D11_PWM/MOSI, Qinterrupt.B
  N4: Arduino.D13/SCK, Rled.Pin_1
  GND: Arduino.GND, VReg.GND, BIP373.drain, Vin.pin2, Frequency.pin1, Qinterrupt.C, LED.cathode, Pad1.pad, Pad2.pad
  N5: Arduino.D2, Activation.pin2
  N6: Arduino.D3_PWM, Vehicle.pin1
  N7: Arduino.D4, Coil.pin2, JMP.pin1
  N8: Arduino.D5_PWM, Activation.pin3
  N9: Arduino.D7, Activation.pin1
  N10: Arduino.5V, Frequency.pin3
  N11: Arduino.VIN, VReg.output_voltage
  N12: VReg.input_voltage, Vin.pin1
  N13: BIP373.gate, JMP.pin2
  N14: BIP373.source, Coil.pin3
  N15: Vehicle.pin2, Qinterrupt.E
  N16: LED.anode, Rled.Pin_0
